# Fritzing sketch alimentacao v3 (saved by Fritzing 0.9.3b)
circuit board: 8.9cm x 6.71056cm
breadboards: 1

parts:
  Geral = Basic FET P-Channel [package="TO220 [THT]"]
  Driver = Basic FET P-Channel [package="TO220 [THT]"]
  5V = Basic FET P-Channel [package="TO220 [THT]"]
  3_3V = Basic FET P-Channel [package="TO220 [THT]"]
  Driver_2 = Power Jack [package=power_jack_slot]
  U2 = RJ45 Jack [package=rj45-8]
  S1 = Pushbutton [package="[THT]"]
  S2 = Pushbutton [package="[THT]"]
  3_3v = female pin header, 2 pins [form="♀ (female)"]
  5v = female pin header, 2 pins [form="♀ (female)"]
  C1 = Electrolytic Capacitor [capacitance=1µF package="200 mil [THT, electrolytic]"]

nets:
  N1: Geral.gate, U2.6
  N2: Geral.drain, Driver.source, 5V.source, 3_3V.source
  N3: Geral.source, U2.8
  N4: Driver.gate, U2.5
  N5: Driver.drain, Driver_2.PWR
  N6: 5V.gate, U2.4
  N7: 5V.drain, U2.7, S1.Pin_3, S1.Pin_4, 5v.pin1
  N8: 3_3V.gate, U2.2
  N9: 3_3V.drain, U2.3, S2.Pin_3, S2.Pin_4, 3_3v.pin1
  N10: Driver_2.GNDBREAK, U2.1, S1.Pin_1, S1.Pin_2, S2.Pin_1, S2.Pin_2, 3_3v.pin2, 5v.pin2, C1.-

notes:
  +

custom parts:
  Pushbutton: A generic pushbutton.
