# Fritzing sketch alimentacao (saved by Fritzing 0.9.3b)
circuit board: 8.03462cm x 6.35424cm
breadboards: 1

parts:
  Geral = Basic FET P-Channel [package="TO220 [THT]"]
  Driver = Basic FET P-Channel [package="TO220 [THT]"]
  5V = Basic FET P-Channel [package="TO220 [THT]"]
  3_3V = Basic FET P-Channel [package="TO220 [THT]"]
  Driver_2 = Power Jack [package=power_jack_slot]
  Bateria = Power Jack [package=power_jack_slot]
  5V_2 = Power Jack [package=power_jack_slot]
  3_3V_2 = Power Jack [package=power_jack_slot]
  U2 = RJ45 Jack [package=rj45-8]
  5Vin = Screw terminal - 2 pins [package=THT]
  3_3out = Screw terminal - 2 pins [package=THT]
  3_3In = Screw terminal - 2 pins [package=THT]
  5Vout = Screw terminal - 2 pins [package=THT]
  R1 = Resistor [tolerance=±5% resistance=0 package=THT]

nets (from the pcb view):
  N1: Geral.gate, U2.6
  N2: Geral.drain, Driver.source, 5V.source, 3_3V.source
  N3: Geral.source, Bateria.PWR, U2.8
  N4: Driver.gate, U2.5
  N5: Driver.drain, Driver_2.PWR
  N6: 5V.gate, U2.4
  N7: 5V.drain, 5Vin.pin2
  N8: 3_3V.gate, U2.2
  N9: 3_3V.drain, 3_3In.pin2
  N10: Driver_2.GNDBREAK, Bateria.GNDBREAK, 5V_2.GNDBREAK, 3_3V_2.GNDBREAK, 3_3out.pin1, 3_3In.pin1, 5Vout.pin1, R1.Pin_1
  N11: 5V_2.PWR, U2.7, 5Vout.pin2
  N12: 3_3V_2.PWR, U2.3, 3_3out.pin2
  N13: U2.1, 5Vin.pin1, R1.Pin_0
