# Fritzing sketch alimentacao2 (saved by Fritzing 0.9.3b)
circuit board: 8.87924cm x 6.72469cm
breadboards: 1

parts:
  Geral = Basic FET P-Channel [package="TO220 [THT]"]
  Driver = Basic FET P-Channel [package="TO220 [THT]"]
  5V = Basic FET P-Channel [package="TO220 [THT]"]
  3_3V = Basic FET P-Channel [package="TO220 [THT]"]
  Driver_2 = Power Jack [package=power_jack_slot]
  Bateria = Power Jack [package=power_jack_slot]
  5V_2 = Power Jack [package=power_jack_slot]
  3_3V_2 = Power Jack [package=power_jack_slot]
  U2 = RJ45 Jack [package=rj45-8]
  R1 = Resistor [tolerance=±5% resistance=0 package=THT]
  S1 = Pushbutton [package="[THT]"]
  S2 = Pushbutton [package="[THT]"]
  R2 = Resistor [tolerance=±5% resistance=0 package=THT]

nets (from the pcb view):
  N1: Geral.gate, U2.6
  N2: Geral.drain, 5V.source, 3_3V.source, R2.Pin_1
  N3: Geral.source, Bateria.PWR, U2.8
  N4: Driver.gate, U2.5
  N5: Driver.drain, Driver_2.PWR
  N6: Driver.source, R2.Pin_0
  N7: 5V.gate, U2.4
  N8: 5V.drain, 5V_2.PWR, U2.7, S1.Pin_3, S1.Pin_4
  N9: 3_3V.gate, U2.2
  N10: 3_3V.drain, 3_3V_2.PWR, U2.3, S2.Pin_3, S2.Pin_4
  N11: Driver_2.GNDBREAK, Bateria.GNDBREAK, 5V_2.GNDBREAK, 3_3V_2.GNDBREAK, U2.1, R1.Pin_0, R1.Pin_1, S1.Pin_1, S1.Pin_2, S2.Pin_1, S2.Pin_2

custom parts:
  Pushbutton: A generic pushbutton.
