# Fritzing sketch painel (saved by Fritzing 0.9.3b)
circuit board: 5.5cm x 5.5cm
breadboards: 1

parts:
  U2 = RJ45 Jack [package=rj45-8]
  Mult3_3 = Header 3 [package=molex-1x3_lock]
  Mult5 = Header 3 [package=molex-1x3_lock]
  Mult15 = Header 3 [package=molex-1x3_lock]
  SW_3_3V = Header 2 [package=molex-1x2_lock]
  Led_3_3V = Header 2 [package=molex-1x2_lock]
  led = Resistor [tolerance=±5% resistance=560 package=THT]
  atalho = Resistor [tolerance=±5% resistance=10k package=THT]
  Led_5V = Header 2 [package=molex-1x2_lock]
  SW_5V = Header 2 [package=molex-1x2_lock]
  led1 = Resistor [tolerance=±5% resistance=560 package=THT]
  atalho1 = Resistor [tolerance=±5% resistance=10k package=THT]
  pull_down1 = Resistor [tolerance=±5% resistance=10k package=THT]
  Led_drive = Header 2 [package=molex-1x2_lock]
  SW_drive = Header 2 [package=molex-1x2_lock]
  led2 = Resistor [tolerance=±5% resistance=560 package=THT]
  atalho2 = Resistor [tolerance=±5% resistance=10k package=THT]
  pull_down2 = Resistor [tolerance=±5% resistance=10k package=THT]
  Led_geral = Header 2 [package=molex-1x2_lock]
  SW_geral = Header 2 [package=molex-1x2_lock]
  led3 = Resistor [tolerance=±5% resistance=560 package=THT]
  atalho3 = Resistor [tolerance=±5% resistance=10k package=THT]
  pull_down3 = Resistor [tolerance=±5% resistance=10k package=THT]
  pull_down = Resistor [tolerance=±5% resistance=10k package=THT]
  R1 = Resistor [tolerance=±5% resistance=0 package=THT]

nets (from the pcb view):
  N1: U2.1, Mult3_3.2, Mult5.2, Mult15.2, SW_3_3V.1, SW_5V.1, SW_drive.1, SW_geral.1
  N2: U2.2, SW_3_3V.2, led.Pin_0, atalho.Pin_0
  N3: U2.3, Mult3_3.3
  N4: U2.4, SW_5V.2, led1.Pin_0, atalho1.Pin_0
  N5: U2.5, SW_drive.2, led2.Pin_0, atalho2.Pin_0
  N6: U2.6, SW_geral.2, led3.Pin_0, atalho3.Pin_0
  N7: U2.7, Mult5.3
  N8: U2.8, pull_down1.Pin_1, pull_down2.Pin_1, pull_down3.Pin_1, pull_down.Pin_1, R1.Pin_1
  N9: Mult3_3.1, Mult5.1, Mult15.1, Mult15.3, R1.Pin_0
  N10: Led_3_3V.1, led.Pin_1
  N11: Led_3_3V.2, atalho.Pin_1, pull_down.Pin_0
  N12: Led_5V.1, led1.Pin_1
  N13: Led_5V.2, atalho1.Pin_1, pull_down1.Pin_0
  N14: Led_drive.1, led2.Pin_1
  N15: Led_drive.2, atalho2.Pin_1, pull_down2.Pin_0
  N16: Led_geral.1, led3.Pin_1
  N17: Led_geral.2, atalho3.Pin_1, pull_down3.Pin_0
