# Fritzing sketch principal (saved by Fritzing 0.9.2b)
circuit board: 10cm x 15cm
breadboards: 1

parts:
  Rasp = Raspberry Pi Zero
  Driver = female pin header, 13 pins [form="♀ (female)"]
  J11 = female pin header, 12 pins [form="♀ (female)"]
  P4B = Power Jack [package=power_jack_slot]
  Part1 = 16-Channel 12-bit PCA9685 PWM/Servo Driver
  P4F = Power Jack [package=power_jack_slot]
  P4E = Power Jack [package=power_jack_slot]
  Not = PICAXE-14M [package=THT]
  Flip_Flop = PICAXE-14M [package=THT]
  5V = Power Jack [package=power_jack_slot]
  3_3 = Power Jack [package=power_jack_slot]
  U1 = RJ45 Jack [package=rj45-8]

nets:
  N1: Rasp.pin_2, Rasp.pin_4, Part1.V+, 5V.PWR
  N2: Rasp.pin_3, Part1.SDA, U1.5
  N3: Rasp.pin_5, Part1.SCL, U1.6
  N4: Rasp.pin_6, Rasp.pin_9, Rasp.pin_39, Driver.pin13, J11.pin7, J11.pin8, P4B.GNDBREAK, Part1.GND, Not.In_0_/_ADC_0, Flip_Flop.Out_2, 5V.GNDBREAK, 3_3.GNDBREAK
  N5: Rasp.pin_11, Driver.pin9
  N6: Rasp.pin_12, Driver.pin7
  N7: Rasp.pin_13, Driver.pin8
  N8: Rasp.pin_16, Flip_Flop.Out_1
  N9: Rasp.pin_18, Flip_Flop.+V, U1.2
  N10: Rasp.pin_22, U1.7
  N11: Rasp.pin_29, Driver.pin4
  N12: Rasp.pin_31, Driver.pin3
  N13: Rasp.pin_33, Driver.pin2
  N14: Rasp.pin_36, Flip_Flop.Out_4
  N15: Rasp.pin_38, Flip_Flop.In_2, U1.4
  N16: Rasp.pin_40, U1.8
  N17: Driver.pin11, Part1.VCC, Not.0V, Flip_Flop.Serial_In, Flip_Flop.In_3_/_Infrain, Flip_Flop.In_1, 3_3.PWR
  N18: J11.pin1, J11.pin2, P4E.PWR
  N19: J11.pin3, J11.pin4, P4E.GNDBREAK
  N20: J11.pin5, J11.pin6, P4B.PWR
  N21: J11.pin9, J11.pin10, P4F.GNDBREAK
  N22: J11.pin11, J11.pin12, P4F.PWR
  N23: Not.+V, Flip_Flop.In_4_/_ADC_4, U1.1
  N24: Not.Serial_In, Flip_Flop.0V
  N25: Not.In_4_/_ADC_4, Flip_Flop.Out_3, U1.3
  N26: Not.In_3_/_Infrain, Flip_Flop.In_0_/_ADC_0

custom parts:
  16-Channel 12-bit PCA9685 PWM/Servo Driver: The Adafruit 16-Channel 12-bit PWM/Servo Driver will drive up to 16 servos over I2C with only 2 pins. The on-board PCA9685 PWM controller will drive all 16 channels simultaneously with no additional processing overhead. What's more, you can chain up to 62 of them to control up to 992 servos - all with the same 2 pins
