# Fritzing sketch sensores v2 (saved by Fritzing 0.9.3b)
circuit board: 9cm x 2.2cm
breadboards: 1

parts:
  Ecoder1power = Header 2 [package=molex-1x2_lock]
  dados = RJ45 Jack [package=rj45-8]
  Ecoder2power = Header 2 [package=molex-1x2_lock]
  Ecoder1signal = Header 2 [package=molex-1x2_lock]
  Ecoder2signal1 = Header 2 [package=molex-1x2_lock]
  Linha1 = Header 3 [package=molex-1x3_lock]
  Linha2 = Header 3 [package=molex-1x3_lock]
  Gyro = female pin header, 10 pins [form="♀ (female)"]
  3_3V = Header 2 [package=molex-1x2_lock]
  5V = Header 2 [package=molex-1x2_lock]
  C1 = Ceramic Capacitor [capacitance=100nF package="100 mil [THT, multilayer]"]
  C2 = Ceramic Capacitor [capacitance=100nF package="100 mil [THT, multilayer]"]
  C3 = Ceramic Capacitor [capacitance=100nF package="100 mil [THT, multilayer]"]
  C4 = Ceramic Capacitor [capacitance=100nF package="100 mil [THT, multilayer]"]

nets:
  N1: Ecoder1power.1, Ecoder2power.1, Linha1.1, Linha2.1, Gyro.pin9, 3_3V.1, 5V.1, C1.0, C2.0, C3.0, C4.1
  N2: Ecoder1power.2, Ecoder2power.2, 5V.2, C2.1, C4.0
  N3: dados.1, Ecoder1signal.1
  N4: dados.2, Ecoder1signal.2
  N5: dados.3, Ecoder2signal1.1
  N6: dados.4, Ecoder2signal1.2
  N7: dados.5, Gyro.pin7
  N8: dados.6, Gyro.pin8
  N9: dados.7, Linha1.3
  N10: dados.8, Linha2.3
  N11: Linha1.2, Linha2.2, Gyro.pin10, 3_3V.2, C1.1, C3.1
