# Fritzing sketch sensores (saved by Fritzing 0.9.3b)
circuit board: 9cm x 2cm
breadboards: 1

parts:
  Ecoder1power = Header 2 [package=molex-1x2_lock]
  dados = RJ45 Jack [package=rj45-8]
  3_3V = Power Jack [package=power_jack_slot]
  Ecoder2power = Header 2 [package=molex-1x2_lock]
  Ecoder1signal = Header 2 [package=molex-1x2_lock]
  Ecoder2signal1 = Header 2 [package=molex-1x2_lock]
  Linha1 = Header 3 [package=molex-1x3_lock]
  Linha2 = Header 3 [package=molex-1x3_lock]
  Gyro = female pin header, 10 pins [form="♀ (female)"]

nets:
  N1: Ecoder1power.1, 3_3V.GNDBREAK, Ecoder2power.1, Linha1.1, Linha2.1, Gyro.pin9
  N2: Ecoder1power.2, 3_3V.PWR, Ecoder2power.2, Linha1.2, Linha2.2, Gyro.pin10
  N3: dados.1, Ecoder1signal.1
  N4: dados.2, Ecoder1signal.2
  N5: dados.3, Ecoder2signal1.1
  N6: dados.4, Ecoder2signal1.2
  N7: dados.5, Gyro.pin7
  N8: dados.6, Gyro.pin8
  N9: dados.7, Linha1.3
  N10: dados.8, Linha2.3
